# Fritzing sketch esp_rika_stove (saved by Fritzing 1.0.2b)

parts:
  Temperature_Probe_DB16 = DB15 Connector [package=db15]
  Stove_DB16 = DB15 Connector [package=db15]
  Composant2 = Logic Level Converter
  U3 = LuaNode32 / ESP32 [part_number=ESP32S-PIN30]

nets:
  N1: Temperature_Probe_DB16.1, Stove_DB16.1, Composant2.HV, U3.Vin
  N2: Temperature_Probe_DB16.4, Stove_DB16.4
  GND: Temperature_Probe_DB16.5, Stove_DB16.5, Composant2.GND, U3.GND
  N3: Temperature_Probe_DB16.15, Stove_DB16.15
  N4: Stove_DB16.2, Composant2.RX_HV
  N5: Stove_DB16.3, Composant2.TX_HV
  N6: Composant2.LV, U3.3V3
  N7: Composant2.RX_LV, U3.RX2
  N8: Composant2.TX_LV, U3.TX2

notes:
  3. Tx
  15. GND
  1. 5V VCC
  2. Rx
  5. GND
  4. TTL
  Stove DB15
  Temperature probe DB15
  DB15 pinout

custom parts:
  DB15 Connector: DB15 Connector Standard DB15 (D-Sub 15) pc midi or gameport connector. Can be used for old PC compatible joystic.
  LuaNode32 / ESP32: New Image for LuaNode32 DOIT ESP32 DEVKIT V1. Base parts from LuaNode32 / ESP32 ESP32 based LuaNode32 by G.Noorlander DOIT Esp32 DevKit v1 (30 pins long, 11 pins width) by Werner Rothschopf (modified by vanepp Dec 2018)
